// Logisim project lab3.circ as structural Verilog: 6 circuits, main circuit Adder_8bit
module Adder_8bit (
  input  [7:0] in_1,
  input  [7:0] in_2,
  output out_3,
  output [7:0] out_4
);

  wire adder_1bit_1_pout, adder_1bit_2_pout, adder_1bit_3_pout, adder_1bit_4_pout, adder_1bit_5_pout,
       adder_1bit_7_pout, adder_1bit_8_pout;

  Adder_1bit adder_1bit_1 (.A(in_2[4]), .B(in_1[4]), .Pin(adder_1bit_3_pout), .S(out_4[4]), .Pout(adder_1bit_1_pout));
  Adder_1bit adder_1bit_2 (.A(in_2[5]), .B(in_1[5]), .Pin(adder_1bit_1_pout), .S(out_4[5]), .Pout(adder_1bit_2_pout));
  Adder_1bit adder_1bit_3 (.A(in_1[3]), .B(in_2[3]), .Pin(adder_1bit_4_pout), .S(out_4[3]), .Pout(adder_1bit_3_pout));
  Adder_1bit adder_1bit_4 (.A(in_1[2]), .B(in_2[2]), .Pin(adder_1bit_7_pout), .S(out_4[2]), .Pout(adder_1bit_4_pout));
  Adder_1bit adder_1bit_5 (.A(in_2[6]), .B(in_1[6]), .Pin(adder_1bit_2_pout), .S(out_4[6]), .Pout(adder_1bit_5_pout));
  Adder_1bit adder_1bit_6 (.A(in_2[7]), .B(in_1[7]), .Pin(adder_1bit_5_pout), .S(out_4[7]), .Pout(out_3));
  Adder_1bit adder_1bit_7 (.A(in_1[1]), .B(in_2[1]), .Pin(adder_1bit_8_pout), .S(out_4[1]), .Pout(adder_1bit_7_pout));
  Adder_1bit adder_1bit_8 (.A(in_1[0]), .B(in_2[0]), .Pin(1'b0), .S(out_4[0]), .Pout(adder_1bit_8_pout));
endmodule

module Adder_1bit (
  input  A,
  input  B,
  input  Pin,
  output S,
  output Pout
);

  wire and_1_out, and_2_out, and_3_out, and_4_out, and_5_out, and_6_out, and_7_out, not_1_out, not_2_out,
       not_3_out;

  not not_1 (not_1_out, A);
  not not_2 (not_2_out, B);
  not not_3 (not_3_out, Pin);
  and and_1 (and_1_out, Pin, not_2_out, not_1_out);
  and and_2 (and_2_out, not_3_out, B, not_1_out);
  and and_3 (and_3_out, not_3_out, not_2_out, A);
  and and_4 (and_4_out, Pin, B, A);
  and and_5 (and_5_out, A, B);
  and and_6 (and_6_out, A, Pin);
  and and_7 (and_7_out, B, Pin);
  or or_1 (S, and_1_out, and_2_out, and_3_out, and_4_out);
  or or_2 (Pout, and_5_out, and_6_out, and_7_out);
endmodule

module _2421BCD (
  input  [3:0] in_1,
  input  [3:0] in_2,
  output [1:0] out_3,
  output [3:0] out_4
);

  wire adder_1_cout;
  wire [3:0] adder_1_out, n2421_bin_1_b0, n2421_bin_2_b0;

  _2421__Bin u_2421_bin_1 (
    .a3(in_1[3]), .a2(in_1[2]), .a1(in_1[1]), .a0(in_1[0]), .b3(n2421_bin_1_b0[3]), .b2(n2421_bin_1_b0[2]),
    .b1(n2421_bin_1_b0[1]), .b0(n2421_bin_1_b0[0]));
  _2421__Bin u_2421_bin_2 (
    .a3(in_2[3]), .a2(in_2[2]), .a1(in_2[1]), .a0(in_2[0]), .b3(n2421_bin_2_b0[3]), .b2(n2421_bin_2_b0[2]),
    .b1(n2421_bin_2_b0[1]), .b0(n2421_bin_2_b0[0]));
  Adder #(.width(4)) adder_1 (
    .a(n2421_bin_1_b0), .b(n2421_bin_2_b0), .out(adder_1_out), .cin(1'b1), .cout(adder_1_cout));
  Bin__2421 bin_2421_1 (
    .cin(adder_1_cout), .a3(adder_1_out[3]), .a2(adder_1_out[2]), .a1(adder_1_out[1]), .a0(adder_1_out[0]),
    .Pout2(out_3[0]), .Pout(out_3[1]), .b3(out_4[3]), .b2(out_4[2]), .b1(out_4[1]), .b0(out_4[0]));
endmodule

module _2421__Bin (
  input  a3,
  input  a2,
  input  a1,
  input  a0,
  output b3,
  output b2,
  output b1,
  output b0
);

  wire and_1_out, and_2_out, and_3_out, and_4_out, and_5_out, and_6_out, and_7_out, and_8_out, and_9_out,
       and_10_out, and_11_out, and_12_out, and_13_out, and_14_out, and_15_out, not_1_out, not_2_out,
       not_3_out, not_4_out, not_5_out, not_6_out, not_7_out, not_8_out, not_9_out, not_10_out, not_11_out,
       not_12_out, not_13_out, not_14_out, not_15_out, not_16_out, not_17_out, not_18_out, not_19_out,
       not_20_out;

  and and_1 (and_1_out, a2, a1);
  and and_2 (and_2_out, a3, not_1_out, not_2_out);
  not not_1 (not_1_out, a2);
  not not_2 (not_2_out, a0);
  not not_3 (not_3_out, a3);
  and and_3 (and_3_out, not_3_out, a2);
  and and_4 (and_4_out, a2, not_4_out);
  not not_4 (not_4_out, a1);
  not not_5 (not_5_out, a2);
  and and_5 (and_5_out, a3, not_5_out, not_6_out);
  not not_6 (not_6_out, a0);
  and and_6 (and_6_out, a3, not_7_out, a1);
  not not_7 (not_7_out, a2);
  not not_8 (not_8_out, a3);
  not not_9 (not_9_out, a2);
  and and_7 (and_7_out, not_8_out, not_9_out, a1);
  not not_10 (not_10_out, a3);
  and and_8 (and_8_out, not_10_out, a2, a0);
  not not_11 (not_11_out, a2);
  and and_9 (and_9_out, a3, not_11_out, not_12_out);
  not not_12 (not_12_out, a0);
  and and_10 (and_10_out, a3, a2, not_13_out);
  not not_13 (not_13_out, a1);
  not not_14 (not_14_out, a3);
  not not_15 (not_15_out, a2);
  not not_16 (not_16_out, a3);
  not not_17 (not_17_out, a0);
  not not_18 (not_18_out, a2);
  not not_19 (not_19_out, a0);
  not not_20 (not_20_out, a2);
  or or_1 (b3, and_1_out, and_2_out);
  or or_2 (b2, and_3_out, and_4_out, and_5_out, and_6_out);
  or or_3 (b1, and_7_out, and_8_out, and_9_out, and_10_out);
  and and_11 (and_11_out, not_14_out, not_15_out, a0);
  and and_12 (and_12_out, not_16_out, a2, a1, not_17_out);
  and and_13 (and_13_out, a3, not_18_out, not_19_out);
  and and_14 (and_14_out, a3, not_20_out, a1);
  and and_15 (and_15_out, a3, a2, a0);
  or or_4 (b0, and_11_out, and_12_out, and_13_out, and_14_out, and_15_out);
endmodule

module Bin__2421 (
  input  cin,
  input  a3,
  input  a2,
  input  a1,
  input  a0,
  output Pout2,
  output Pout,
  output b3,
  output b2,
  output b1,
  output b0
);

  wire and_1_out, and_2_out, and_3_out, and_4_out, and_5_out, and_6_out, and_7_out, and_8_out, and_9_out,
       and_10_out, and_11_out, and_12_out, and_13_out, and_14_out, and_15_out, and_16_out, and_17_out,
       and_18_out, and_19_out, and_20_out, and_21_out, and_22_out, and_23_out, and_24_out, and_25_out,
       not_1_out, not_2_out, not_3_out, not_4_out, not_5_out, not_6_out, not_7_out, not_8_out, not_9_out,
       not_10_out, not_11_out, not_12_out, not_13_out, not_14_out, not_15_out, not_16_out, not_17_out,
       not_18_out, not_19_out, not_20_out, not_21_out, not_22_out, not_23_out, not_24_out, not_25_out,
       not_26_out, not_27_out, not_28_out, not_29_out;

  and and_1 (and_1_out, a3, a1);
  and and_2 (and_2_out, a3, a2);
  not not_1 (not_1_out, a3);
  not not_2 (not_2_out, a1);
  not not_3 (not_3_out, a3);
  not not_4 (not_4_out, a2);
  not not_5 (not_5_out, a0);
  not not_6 (not_6_out, a0);
  not not_7 (not_7_out, a3);
  not not_8 (not_8_out, a1);
  not not_9 (not_9_out, a2);
  not not_10 (not_10_out, a2);
  not not_11 (not_11_out, cin);
  not not_12 (not_12_out, a3);
  not not_13 (not_13_out, a2);
  not not_14 (not_14_out, a3);
  not not_15 (not_15_out, a2);
  not not_16 (not_16_out, a3);
  not not_17 (not_17_out, a1);
  not not_18 (not_18_out, a2);
  not not_19 (not_19_out, a1);
  not not_20 (not_20_out, a1);
  not not_21 (not_21_out, a0);
  not not_22 (not_22_out, a0);
  not not_23 (not_23_out, a3);
  not not_24 (not_24_out, a2);
  not not_25 (not_25_out, a1);
  not not_26 (not_26_out, cin);
  not not_27 (not_27_out, a1);
  not not_28 (not_28_out, a0);
  not not_29 (not_29_out, a0);
  or or_1 (Pout, and_1_out, and_2_out, cin);
  and and_3 (and_3_out, a2, a0);
  and and_4 (and_4_out, not_1_out, a2, a1);
  and and_5 (and_5_out, a3, not_2_out);
  and and_6 (and_6_out, cin, not_3_out, not_4_out);
  and and_7 (and_7_out, cin, a3, not_5_out);
  and and_8 (and_8_out, a2, not_6_out);
  and and_9 (and_9_out, not_7_out, a2, a1);
  and and_10 (and_10_out, a3, not_8_out);
  and and_11 (and_11_out, a3, not_9_out, a0);
  and and_12 (and_12_out, cin, not_10_out);
  and and_13 (and_13_out, cin, a3);
  and and_14 (and_14_out, not_11_out, not_12_out, not_13_out, a1);
  and and_15 (and_15_out, not_14_out, not_15_out, a1, a0);
  and and_16 (and_16_out, not_16_out, a2, not_17_out, a0);
  and and_17 (and_17_out, a3, not_18_out, not_19_out);
  and and_18 (and_18_out, a3, not_20_out, not_21_out);
  and and_19 (and_19_out, a3, a2, a1, a0);
  and and_20 (and_20_out, cin, a3, not_22_out);
  and and_21 (and_21_out, not_23_out, a0);
  and and_22 (and_22_out, not_24_out, not_25_out, a0);
  and and_23 (and_23_out, not_26_out, a2, a1, a0);
  and and_24 (and_24_out, a3, a2, not_27_out, not_28_out);
  and and_25 (and_25_out, cin, a3, a1, not_29_out);
  or or_2 (b3, and_3_out, and_4_out, and_5_out, and_6_out, and_7_out);
  or or_3 (b2, and_8_out, and_9_out, and_10_out, and_11_out, and_12_out, and_13_out);
  or or_4 (b1, and_14_out, and_15_out, and_16_out, and_17_out, and_18_out, and_19_out, and_20_out);
  or or_5 (b0, and_21_out, and_22_out, and_23_out, and_24_out, and_25_out);

  assign Pout2 = 1'b0;
endmodule

module T_trigger (
  output [2:0] out_1
);

  wire and_1_out, clock_1_out;

  T_Flip_Flop t_ff_1 (.clk(clock_1_out), .T(and_1_out), .Q(out_1[2]));  // open: Qn, preset, reset, en
  and and_1 (and_1_out, out_1[1], out_1[0]);
  T_Flip_Flop t_ff_2 (.clk(clock_1_out), .T(out_1[0]), .Q(out_1[1]));  // open: Qn, preset, reset, en
  Clock clock_1 (.out(clock_1_out));
  T_Flip_Flop t_ff_3 (.clk(clock_1_out), .T(1'b1), .Q(out_1[0]));  // open: Qn, preset, reset, en
endmodule
